# Fritzing sketch SmartCooker (saved by Fritzing 1.0.2b)
breadboards: 3

parts:
  Breadboard4 = Breadboard Split Power
  Breadboard5 = Breadboard Split Power
  A1 = Particle - Photon2
  DFPlayer_Mini1 = DFPlayer MINI [package="DIP (Dual Inline) [THT]"]
  S1 = Pushbutton [package="[THT]"]
  Part1 = 12 NeoPixel Ring [part_number=1643]
  OLED_I2C1 = OLED 128x64 I2C Monochrome Display
  S2 = Pushbutton [package="[THT]"]
  S3 = Pushbutton [package="[THT]"]
  NFC_Controller = Header 4 [package=screwterminal-3.5mm-4_lock]
  Relay1 = Relay - 6 pins [package="DIP (Dual Inline) [THT]"]
  A2 = MAX6675 module [package=THT]
  R1 = Resistor [tolerance=±5% power=0.25W resistance=10000 package=THT]
  SP1 = SPEAKER [package=pcb_mount_speaker]
  Q1 = PNP-Transistor [package="TO92 [THT]"]
  R2 = Resistor [tolerance=±5% power=0.25W resistance=220 package=THT]
  R3 = Resistor [tolerance=±5% power=0.25W resistance=220 package=THT]
  A3 = nozzle-bolt style thermocouple [package=THT]
  Oven = Dryer heater
  Hall_Effect_Sensor = KY-003 Hall Magnetic Sensor Module [package="Breakout board"]
  Outlet = 120V duplex outlet_1  # not connected

nets:
  GND: Breadboard4.pin3Z, Breadboard4.pin20Z, Breadboard4.pin29Z, Breadboard5.pin3Z, Breadboard5.pin11Z, Breadboard5.pin28Z, A1.Pin_4, A1.Pin_30, S1.Pin_3, S1.Pin_4, Part1.GND, OLED_I2C1.GND, S3.Pin_3, S3.Pin_4, NFC_Controller.1, Relay1.GND, A2.pin1, R1.Pin_1, Q1.B, R3.Pin_0, Hall_Effect_Sensor.-
  N1: Breadboard4.pin5Y, S2.Pin_3, S2.Pin_4
  N2: Breadboard4.pin21Y, Breadboard4.pin29Y, Breadboard5.pin3Y, Breadboard5.pin15Y, Breadboard5.pin17Y, Breadboard5.pin29Y, OLED_I2C1.VDD, NFC_Controller.2
  VCC: A1.Pin_2, Relay1.VCC, A2.pin2, Hall_Effect_Sensor.Vin
  N3: A1.Pin_5, S2.Pin_1, S2.Pin_2, R1.Pin_0
  N4: A1.Pin_9, Hall_Effect_Sensor.S
  N5: A1.Pin_10, A2.pin4
  N6: A1.Pin_11, A2.pin3
  N7: A1.Pin_13, A2.pin5
  N8: A1.Pin_14, DFPlayer_Mini1.TX
  N9: A1.Pin_15, DFPlayer_Mini1.RX
  N10: A1.Pin_17, OLED_I2C1.SDA, NFC_Controller.4
  N11: A1.Pin_18, OLED_I2C1.SCK
  N12: A1.Pin_19, Part1.IN
  N13: A1.Pin_21, Q1.C, R3.Pin_1
  N14: A1.Pin_26, R2.Pin_0
  N15: DFPlayer_Mini1.SPK1, SP1.-
  N16: DFPlayer_Mini1.SPK2, SP1.+
  N17: DFPlayer_Mini1.IO_1, S3.Pin_1, S3.Pin_2
  N18: DFPlayer_Mini1.IO_2, S1.Pin_1, S1.Pin_2
  N19: Relay1.IN, Q1.E, R2.Pin_1
  N20: Relay1.COM, Oven.Pin_2
  N21: Relay1.ON, Oven.Pin_1
  N22: A2.pin6, A3.pin2
  N23: A2.pin7, A3.pin1

notes:
  NFC Controller
  Hot wire split between common and NO then plugged into the wall outlet
  Buttons for Vol Control
  The oven is also plugged into the outlet

custom parts:
  Breadboard Split Power: A custom 6 pin per group power supply strip where the top row (ground) is all bussed together and the bottom row (+V) is split in two groups of 12 pins. This version is modified to be a loadable part and was rescaled to be on the standard 1px = 1thou grid with the size set in inches
  Particle - Photon2: The Photon 2 is a microcontroller and Wi-Fi networking developed by particle. Features: 802.11a/b/g/n Wi-Fi, 2.4 GHz and 5 GHz Integrated PCB antenna Integrated U.FL connector for external antenna Integrated RF switch BLE 5 using same antenna as Wi-Fi Realtek RTL8721DM MCU ARM Cortex M33 CPU, 200 MHz 2048 KB (2 MB) user application maximum size 3072 KB (3 MB) of RAM available to user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
  DFPlayer MINI: MP3 module by DFRobot.com for playing Music from an SD-Card. Supports WAV and MP3 files.
  Pushbutton: A generic pushbutton.
  12 NeoPixel Ring: 12 ultra bright smart LED NeoPixels are arranged in a circle with 1.5" (37mm) outer diameter. The rings are 'chainable' - connect the output pin of one to the input pin of another. Use only one microcontroller pin to control as many as you can chain together! Each LED is addressable as the driver chip is inside the LED. Each one has ~18mA constant current drive so the color will be very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
  Pushbutton: A generic pushbutton.
  Relay - 6 pins: A DIP stand-in part for whatever IC you want. With 6 pins on a 900mil dual inline package (DIP) footprint.
  MAX6675 module: MAX6675 Module + K Type Thermocouple Sensor Temperature Degrees.
  nozzle-bolt style thermocouple: Generic nozzle-bolt style thermocouple.
  Dryer heater: Dryer heater.
  KY-003 Hall Magnetic Sensor Module: KEYES KY-003 Arduino Hall Magnetic Sensor Module is a switch that will turn on/off in the presence of a magnetic field.
  120V duplex outlet_1: 120V duplex outlet.
